# Fritzing sketch 4-bit_ALU (saved by Fritzing 0.9.3b)
breadboards: 3

parts:
  U1 = 7427 3 x 3 Input NOR Gate [part_number=7427 package="DIP (Dual Inline) [THT]"]
  U2 = 7474 Dual Positive Edge Triggered D Flip Flop [part_number=7474 package="DIP (Dual Inline) [THT]"]
  U3 = 74161 4 Bit Synchronous Up Down Counter [part_number=74161 package="DIP16 [THT]"]
  S1 = Pushbutton [package="[SMD]"]
  R1 = Resistor [tolerance=±5% resistance=220 package=THT]
  R2 = Resistor [tolerance=±5% resistance=220 package=THT]
  R3 = Resistor [tolerance=±5% resistance=220 package=THT]
  R4 = Resistor [tolerance=±5% resistance=220 package=THT]
  R5 = Resistor [tolerance=±5% resistance=220 package=THT]
  R6 = Resistor [tolerance=±5% resistance=220 package=THT]
  U4 = 74153 Dual 4:1 MUX [part_number=74153 package="DIP16 [THT]"]
  U5 = 7400 4 x 2 Input NAND Gate [part_number=7400 package="DIP (Dual Inline) [THT]"]  # not connected
  U6 = 7486 4 x 2 Input XOR Gate [part_number=7486 package="DIP (Dual Inline) [THT]"]  # not connected
  U7 = 74153 Dual 4:1 MUX [part_number=74153 package="DIP16 [THT]"]
  R7 = Resistor [tolerance=±5% resistance=220 package=THT]
  R9 = Resistor [tolerance=±5% resistance=220 package="2010 [SMD]"]
  R10 = Resistor [tolerance=±5% resistance=220 package="2010 [SMD]"]
  R11 = Resistor [tolerance=±5% resistance=220 package="2010 [SMD]"]
  R12 = Resistor [tolerance=±5% resistance=220 package="2010 [SMD]"]
  R13 = Resistor [tolerance=±5% resistance=220 package="2010 [SMD]"]
  R14 = Resistor [tolerance=±5% resistance=220 package=THT]
  U8 = 74153 Dual 4:1 MUX [part_number=74153 package="DIP16 [THT]"]
  U9 = 74195 4 Bit Parallel Access Shift Register [part_number=74195 package="DIP16 [THT]"]
  U10 = 74195 4 Bit Parallel Access Shift Register [part_number=74195 package="DIP16 [THT]"]
  S2 = Pushbutton [package="[SMD]"]
  U11 = 7486 4 x 2 Input XOR Gate [part_number=7486 package="DIP (Dual Inline) [THT]"]
  S3 = Pushbutton [package="[SMD]"]
  U12 = 7400 4 x 2 Input NAND Gate [part_number=7400 package="DIP (Dual Inline) [THT]"]
  R15 = Resistor [tolerance=±5% resistance=220 package=THT]
  R16 = Resistor [tolerance=±5% resistance=220 package=THT]
  R17 = Resistor [tolerance=±5% resistance=220 package=THT]
  R18 = Resistor [tolerance=±5% resistance=220 package=THT]
  R19 = Resistor [tolerance=±5% resistance=220 package=THT]
  R20 = Resistor [tolerance=±5% resistance=220 package=THT]
  R21 = Resistor [tolerance=±5% resistance=220 package=THT]
  R22 = Resistor [tolerance=±5% resistance=220 package=THT]
  R23 = Resistor [tolerance=±5% resistance=220 package=THT]
  D1 = LED_BARGRAPH_10 [package=led_bargaph_10]
  R24 = Resistor [tolerance=±5% resistance=220 package="1206 [SMD]"]  # not connected
  R25 = Resistor [tolerance=±5% resistance=220 package="1206 [SMD]"]
  R26 = Resistor [tolerance=±5% resistance=220 package="1206 [SMD]"]
  R27 = Resistor [tolerance=±5% resistance=220 package="1206 [SMD]"]
  R28 = Resistor [tolerance=±5% resistance=220 package="1206 [SMD]"]
  R29 = Resistor [tolerance=±5% resistance=220 package="1206 [SMD]"]
  R30 = Resistor [tolerance=±5% resistance=220 package="1206 [SMD]"]
  R31 = Resistor [tolerance=±5% resistance=220 package="1206 [SMD]"]
  R32 = Resistor [tolerance=±5% resistance=220 package="1206 [SMD]"]
  R33 = Resistor [tolerance=±5% resistance=220 package="1206 [SMD]"]
  SW2 = DIP Switch 8 Position [package=dipswitch-08]
  SW3 = DIP Switch 8 Position [package=dipswitch-08]
  R34 = Resistor [tolerance=±5% resistance=220 package="2010 [SMD]"]
  R35 = Resistor [tolerance=±5% resistance=220 package="2010 [SMD]"]
  R36 = Resistor [tolerance=±5% resistance=220 package="2010 [SMD]"]
  R37 = Resistor [tolerance=±5% resistance=220 package="2010 [SMD]"]
  R38 = Resistor [tolerance=±5% resistance=220 package="2010 [SMD]"]
  R39 = Resistor [tolerance=±5% resistance=220 package="2010 [SMD]"]
  R40 = Resistor [tolerance=±5% resistance=220 package="2010 [SMD]"]
  R41 = Resistor [tolerance=±5% resistance=220 package="2010 [SMD]"]
  R42 = Resistor [tolerance=±5% resistance=220 package="2010 [SMD]"]
  R43 = Resistor [tolerance=±5% resistance=220 package="2010 [SMD]"]
  R44 = Resistor [tolerance=±5% resistance=220 package="2010 [SMD]"]
  R45 = Resistor [tolerance=±5% resistance=220 package="2010 [SMD]"]
  R46 = Resistor [tolerance=±5% resistance=220 package="2010 [SMD]"]
  R47 = Resistor [tolerance=±5% resistance=220 package="2010 [SMD]"]
  R48 = Resistor [tolerance=±5% resistance=220 package="2010 [SMD]"]
  R49 = Resistor [tolerance=±5% resistance=220 package="2010 [SMD]"]

nets:
  N1: U1.A1, R2.Pin_1
  N2: U1.B1, S1.Pin_3, S1.Pin_4, U4.A0, R13.Pin_1
  N3: U1.Q1, U1.A4
  N4: U1.Q2, R7.Pin_1
  N5: U1.A2, U1.A3
  N6: U1.B2, U2.B1, U3.1
  GND: U1.GND, U2.GND, U3.GND, R2.Pin_0, U4.GND, U7.GND, R7.Pin_0, R9.Pin_0, R13.Pin_0, U8.GND, U9.GND, U9.10, U10.GND, U11.GND, U12.GND, R15.Pin_0, R17.Pin_1, R18.Pin_0, R19.Pin_1, R22.Pin_0, R23.Pin_0, R25.Pin_1, R26.Pin_1, R27.Pin_1, R28.Pin_1, R29.Pin_1, R30.Pin_1, R31.Pin_1, R32.Pin_1, R33.Pin_1, SW2.1, SW2.2, SW2.3, SW2.4, SW2.5, SW2.6, SW2.7, SW2.8, SW3.1, SW3.2, SW3.3, SW3.4, SW3.5, SW3.6, SW3.7, SW3.8
  N7: U1.B3, U2.A3
  N8: U1.Q3, U3.14, U4.S0
  N9: U1.Q4, U3.13, U4.S1
  N10: U1.B4, U2.B3
  VCC: U1.VDD, U2.VDD, U3.VCC, S1.Pin_1, S1.Pin_2, R1.Pin_1, R3.Pin_0, R4.Pin_0, R5.Pin_1, R6.Pin_1, U4.VCC, U7.VCC, R10.Pin_0, R11.Pin_0, R12.Pin_0, U8.VCC, U9.VCC, U10.VCC, S2.Pin_1, S2.Pin_2, U11.VDD, S3.Pin_1, S3.Pin_2, U12.VDD, R16.Pin_0, R20.Pin_0, R21.Pin_0, R34.Pin_0, R35.Pin_0, R36.Pin_0, R37.Pin_0, R38.Pin_0, R39.Pin_0, R40.Pin_0, R41.Pin_0, R42.Pin_0, R43.Pin_0, R44.Pin_0, R45.Pin_0, R46.Pin_0, R47.Pin_0, R48.Pin_0, R49.Pin_0
  N11: U2.A1, R3.Pin_1
  N12: U2.Q1, U2.Q4, U3.2, U8.B1, U9.11
  N13: U2.Q2, R4.Pin_1
  N14: U2.A2, U11.A1, U11.Q2
  N15: U2.B2, U12.A1, U12.B4
  N16: U2.Q3, R6.Pin_0
  N17: U2.A4, U4.Y0
  N18: U2.B4, R5.Pin_0
  N19: U3.7, U3.9, U3.10, R1.Pin_0
  N20: U4.D0, R10.Pin_1
  N21: U4.G1, R14.Pin_0
  N22: U4.C0, R11.Pin_1
  N23: U4.G0, R9.Pin_1
  N24: U4.B0, R12.Pin_1
  N25: U7.D0, R16.Pin_1
  N26: U7.G1, R17.Pin_0
  N27: U7.G0, R15.Pin_1
  N28: U8.G1, R19.Pin_0
  N29: U8.G0, R18.Pin_1
  N30: U9.1, R20.Pin_1
  N31: U9.3, U10.3, SW2.12, R49.Pin_1
  N32: U9.4, U10.4, SW2.16, R34.Pin_1
  N33: U9.5, U10.5, SW2.15, R35.Pin_1
  N34: U9.6, U10.6, SW2.14, R36.Pin_1
  N35: U9.9, U11.Q1
  N36: U10.1, R21.Pin_1
  N37: U10.9, U11.B2
  N38: U10.10, U12.A3
  N39: S2.Pin_3, S2.Pin_4, U11.B1, U12.B1, R23.Pin_1
  N40: U11.A2, S3.Pin_3, S3.Pin_4, U12.A4, R22.Pin_1
  N41: U12.Q1, U12.Q2, U12.A2
  N42: U12.B3, U12.Q3, U12.Q4
  N43: D1.A_A, R29.Pin_0
  N44: D1.B_A, R30.Pin_0
  N45: D1.C_A, R31.Pin_0
  N46: D1.D_A, R28.Pin_0
  N47: D1.E_A, R27.Pin_0
  N48: D1.F_A, R33.Pin_0
  N49: D1.G_A, R26.Pin_0
  N50: D1.H_A, R25.Pin_0
  N51: D1.J_A, R32.Pin_0
  N52: SW2.9, R40.Pin_1
  N53: SW2.10, R39.Pin_1
  N54: SW2.11, R38.Pin_1
  N55: SW2.13, R37.Pin_1
  N56: SW3.9, R47.Pin_1
  N57: SW3.10, R46.Pin_1
  N58: SW3.11, R45.Pin_1
  N59: SW3.12, R44.Pin_1
  N60: SW3.13, R43.Pin_1
  N61: SW3.14, R48.Pin_1
  N62: SW3.15, R42.Pin_1
  N63: SW3.16, R41.Pin_1

notes:
  Compute Unit:
  x1 4:1 MUX
  x3 2 Input XOR
  x4 2 Input NAND
  ----------------------
  Extra:
  x1 4:1 MUX
  x1 2 Input XOR
  *** 3 Chips ***
  Routing Unit:
  x2 4:1 MUX
  ----------------------
  Extra:
  *** 1 Chip ***
  Register Unit:
  x2 Shift Registers
  x4 2 Input NAND
  x2 2 Input XOR
  --------------------------
  Extra:
  *** 4 Chips ***
  Control Unit:
  x1 Counter
  x3 Triple Input NOR
  --------------------------
  Extra:
  *** 2 Chips ***
  Flip - Flops:
  Right: Q
  Left: S
  S'
  Control Unit
  Registers:
  Top: A
  Botton: B
  Buttons:
  Load A
  Load B
  Compute Unit Logic
  Routing Unit
  Compute Unit MUX
  Load / Shift Logic
  Q+ Logic
  S Logic

custom parts:
  7427 3 x 3 Input NOR Gate: 7427 3 x 2 Input NOR Gate
  74153 Dual 4:1 MUX: 74153 Dual 4:1 Multiplexor
